# Fritzing sketch brain (saved by Fritzing 0.8.0b)
perfboards: 1

parts:
  IC1 = IC, DIP package, 14 pins [chip_label=ATTiny84]
  J1 = 7-pin header with pin 5 disabled [form="♀ (female rounded)" package=THT]
  C2 = Ceramic Capacitor [package="100 mil [THT, multilayer]"]
  C3 = Ceramic Capacitor [package="100 mil [THT, multilayer]"]
  J2 = rounded female pin header, 5 pins [form="♀ (female rounded)"]
  XTAL1 = Crystal [frequency="16 Mhz" package=THT]
  J3 = shrouded pin header, 6 pins [form="♂ (shrouded male)"]
  R1 = Resistor [tolerance=±5% resistance=220 package=THT]
  J4 = female pin header, 2 pins [form="♀ (female)"]
  C4 = Electrolytic Capacitor [capacitance=47µF package="100 mil [THT, electrolytic]"]

nets:
  N1: IC1.pin1, J1.pin7, J2.pin4, J3.pin6, R1.Pin_0, J4.pin2, C4.+
  N2: IC1.pin2, C2.1, XTAL1.pin_1
  N3: IC1.pin3, C3.1, XTAL1.pin_0
  N4: IC1.pin4, J3.pin3, R1.Pin_1
  N5: IC1.pin5, J2.pin1
  N6: IC1.pin6, J2.pin2
  N7: IC1.pin7, J2.pin3, J3.pin5
  N8: IC1.pin8, J1.pin4, J3.pin1
  N9: IC1.pin9, J1.pin3, J3.pin2
  N10: IC1.pin10, J1.pin2
  N11: IC1.pin11, J1.pin1
  N12: IC1.pin12, IC1.pin13, IC1.pin14, J1.pin6, C2.0, C3.0, J2.pin5, J3.pin4, J4.pin1, C4.-

notes:
  brain
  Build your own!
  woozle.org/derby
  +

custom parts:
  7-pin header with pin 5 disabled: Generic rounded female header
  Ceramic Capacitor: 100 nF multilayer Ceramic Capacitor
