# Fritzing sketch driver (saved by Fritzing 0.7.12b)
breadboards: 1

parts:
  IC1 = IC, DIP package, 28 pins [chip_label=TLC5941]
  R1 = Resistor [tolerance=±5% resistance=100 package=THT]
  J1 = rounded female pin header, 8 pins [form="♀ (female rounded)"]
  J2 = rounded female pin header, 8 pins [form="♀ (female rounded)"]
  J4 = 7-pin header with pin 5 disabled [form="♀ (female rounded)" package=THT]
  J3 = 7-pin header with pin 5 disabled [form="♀ (female rounded)" package=THT]

nets:
  N1: IC1.pin1, J1.pin2
  N2: IC1.pin2, J1.pin3
  N3: IC1.pin3, J1.pin4
  N4: IC1.pin4, J1.pin5
  N5: IC1.pin5, J1.pin6
  N6: IC1.pin6, J1.pin7
  N7: IC1.pin7, J1.pin8
  N8: IC1.pin8, J2.pin1
  N9: IC1.pin9, J2.pin2
  N10: IC1.pin10, J2.pin3
  N11: IC1.pin11, J2.pin4
  N12: IC1.pin12, J2.pin5
  N13: IC1.pin13, J2.pin6
  N14: IC1.pin14, J2.pin7
  N15: IC1.pin15, J2.pin8
  N16: IC1.pin16, IC1.pin22, R1.Pin_1, J4.pin6, J3.pin6
  N17: IC1.pin17, J4.pin2
  N18: IC1.pin18, IC1.pin19, IC1.pin25, J4.pin3, J3.pin3
  N19: IC1.pin20, R1.Pin_0
  N20: IC1.pin21, J4.pin7, J3.pin7
  N21: IC1.pin23, IC1.pin24, J4.pin4, J3.pin4
  N22: IC1.pin26, J3.pin2
  N23: IC1.pin27, J4.pin1, J3.pin1
  N24: IC1.pin28, J1.pin1

notes:
  woozle.org/derby
  driver
  Build your own!
  digits

custom parts:
  7-pin header with pin 5 disabled: Generic rounded female header
